// Digital circuit lab2_part1.dig as structural Verilog
module lab2_part1 (
  input  inA_0,
  input  inA_1,
  input  inA_2,
  input  inA_3,
  input  inB_0,
  input  inB_1,
  input  inB_2,
  input  inB_3,
  output out0,
  output out1,
  output out2,
  output out3
);

  wire inM_00, inM_01, inM_02, inM_03;

  Multiplexer multiplexer_1 (.sel(inB_0), .in_0(inA_0), .in_1(inA_3), .out(inM_03));
  Multiplexer multiplexer_2 (.sel(inB_0), .in_0(inA_1), .in_1(inA_0), .out(inM_02));
  Multiplexer multiplexer_3 (.sel(inB_0), .in_0(inA_2), .in_1(inA_1), .out(inM_01));
  Multiplexer multiplexer_4 (.sel(inB_0), .in_0(inA_3), .in_1(inA_2), .out(inM_00));
  Multiplexer multiplexer_5 (.sel(inB_1), .in_0(inM_03), .in_1(inM_01), .out(out0));
  Multiplexer multiplexer_6 (.sel(inB_1), .in_0(inM_02), .in_1(inM_00), .out(out1));
  Multiplexer multiplexer_7 (.sel(inB_1), .in_0(inM_01), .in_1(inM_03), .out(out2));
  Multiplexer multiplexer_8 (.sel(inB_1), .in_0(inM_00), .in_1(inM_02), .out(out3));

  // Other names for the same wires on the sheet: inM_10 = out3; inM_11 = out2; inM_12 = out1; inM_13 = out0

  // Notes on the sheet:
  //   Interface (do not edit the content inside this box)
  //   Inputs
  //   Outputs
  //   Rotatee:
  //   Rotation amount:
  //   Result of Rotating  input A by the amount given by input B:
endmodule

/* Test case:
inA_3 inA_2 inA_1 inA_0 inB_3 inB_2 inB_1 inB_0  out3 out2 out1 out0
 0     0     0     0     0     0      0     0      0    0    0    0  
 0     0     0     1     0     0      0     0      0    0    0    1  
 0     0     0     1     0     0      0     1      0    0    1    0  
 0     0     0     1     0     0      1     0      0    1    0    0  
 0     0     0     1     0     0      1     1      1    0    0    0   
 0     1     0     1     0     0      0     0      0    1    0    1  
 0     1     0     1     0     0      0     1      1    0    1    0  
 0     1     0     1     0     0      1     0      0    1    0    1  
 0     1     0     1     0     0      1     1      1    0    1    0 
 1     1     0     1     1     1      1     1      1    1    1    0   
*/
