// Digital circuit lab2_part2.dig as structural Verilog
module lab2_part2 (
  input  in0,
  input  in1,
  input  in2,
  input  in3,
  output seg_a,
  output seg_f,
  output seg_b,
  output seg_g,
  output seg_e,
  output seg_c,
  output seg_d,
  output seg_dp,
  output sign_a,
  output sign_f,
  output sign_b,
  output sign_g,
  output sign_e,
  output sign_c,
  output sign_d,
  output sign_dp
);

  wire [4:1] in_28;
  wire [5:0] in_23;
  wire [5:4] in_26;
  wire [6:0] in_24, in_25, in_29, in_31;
  wire [6:1] in_27;
  wire [6:3] in_30;

  Multiplexer #(.Selector_Bits(4), .Bits(7)) multiplexer_1 (
    .sel({in0, in1, in2, in3}), .in_0({in0, in_23}), .in_1(in_31),
    .in_2({in_27[6:5], {2{in0}}, in_27[2:1], in0}), .in_3({in_27[6:5], {2{in0}}, in_27[2:1], in0}),
    .in_4({in_25[6], in0, in_25[4:3], in0, in_25[1:0]}), .in_5({in_29[6:2], in0, in_29[0]}),
    .in_6({in_29[6:2], in0, in_29[0]}), .in_7({in_25[6], in0, in_25[4:3], in0, in_25[1:0]}),
    .in_8({in_24[6:3], {2{in0}}, in_24[0]}), .in_9({in_30, {3{in0}}}),
    .in_10({{2{in0}}, in_28[4], {2{in0}}, in_28[1], in0}), .in_11({in0, in_26, {4{in0}}}),
    .in_12({in0, in_26, {4{in0}}}), .in_13({{2{in0}}, in_28[4], {2{in0}}, in_28[1], in0}),
    .in_14({in_30, {3{in0}}}), .in_15({in_24[6:3], {2{in0}}, in_24[0]}),
    .out({seg_g, seg_f, seg_e, seg_d, seg_c, seg_b, seg_a}));
  not not_1 (seg_dp, 1'b1);
  not not_2 (sign_a, 1'b1);
  not not_3 (sign_b, 1'b1);
  not not_4 (sign_c, 1'b1);
  not not_5 (sign_d, 1'b1);
  not not_6 (sign_e, 1'b1);
  not not_7 (sign_f, 1'b1);
  not not_8 (sign_dp, 1'b1);
  not not_9 (in_23[0], in0);
  not not_10 (in_23[1], in0);
  not not_11 (in_23[2], in0);
  not not_12 (in_23[3], in0);
  not not_13 (in_23[4], in0);
  not not_14 (in_23[5], in0);
  not not_15 (in_24[0], in0);
  not not_16 (in_24[3], in0);
  not not_17 (in_24[4], in0);
  not not_18 (in_24[5], in0);
  not not_19 (in_24[6], in0);
  not not_20 (in_25[0], in0);
  not not_21 (in_25[1], in0);
  not not_22 (in_25[3], in0);
  not not_23 (in_25[4], in0);
  not not_24 (in_25[6], in0);
  not not_25 (in_26[4], in0);
  not not_26 (in_26[5], in0);
  not not_27 (in_27[1], in0);
  not not_28 (in_27[2], in0);
  not not_29 (in_27[5], in0);
  not not_30 (in_27[6], in0);
  not not_31 (in_28[1], in0);
  not not_32 (in_28[4], in0);
  not not_33 (in_29[0], in0);
  not not_34 (in_29[2], in0);
  not not_35 (in_29[3], in0);
  not not_36 (in_29[4], in0);
  not not_37 (in_29[5], in0);
  not not_38 (in_29[6], in0);
  not not_39 (in_30[3], in0);
  not not_40 (in_30[4], in0);
  not not_41 (in_30[5], in0);
  not not_42 (in_30[6], in0);
  not not_43 (in_31[0], in0);
  not not_44 (in_31[1], in0);
  not not_45 (in_31[2], in0);
  not not_46 (in_31[3], in0);
  not not_47 (in_31[4], in0);
  not not_48 (in_31[5], in0);
  not not_49 (in_31[6], in0);
  Seven_Seg seven_seg_1 (.a(sign_a), .b(sign_b), .c(sign_c), .d(sign_d), .e(sign_e), .f(sign_f), .g(in3), .dp(sign_dp));
  Seven_Seg seven_seg_2 (.a(seg_a), .b(seg_b), .c(seg_c), .d(seg_d), .e(seg_e), .f(seg_f), .g(seg_g), .dp(seg_dp));

  assign sign_g = in3;

  // Other names for the same wires on the sheet: in_23[6] = in0; in_24[2:1] = {2{in0}}; in_25 (some bits) = {2{in0}};
  //   in_26 (some bits) = {5{in0}}; in_27 (some bits) = {3{in0}}; in_28 (some bits) = {5{in0}}; in_29[1] = in0;
  //   in_30[2:0] = {3{in0}}

  // Notes on the sheet:
  //   Interface (do not edit the content inside this box)
  //   Outputs:
  //   Inputs
  //   Sign
  //   Decimal Number
endmodule

/* Test case:
in3 in2 in1 in0  sign_a sign_b sign_c sign_d sign_e sign_f sign_g  seg_a seg_b seg_c seg_d seg_e seg_f seg_g
 0   0   0   0    0      0      0      0      0      0      0       1     1     1     1     1     1     0
*/
