// Digital circuit lab2_part3.dig as structural Verilog
module lab2_part3 (
  input  clk,
  input  in0,
  input  in1,
  input  in2,
  input  in3,
  input  sel_write_1,
  input  sel_write_0,
  input  sel_readA_1,
  input  sel_readA_0,
  input  sel_readB_1,
  input  sel_readB_0,
  output out0,
  output out1,
  output out2,
  output out3,
  output reg0_0,
  output reg0_1,
  output reg0_2,
  output reg0_3,
  output reg1_0,
  output reg1_1,
  output reg1_2,
  output reg1_3,
  output reg2_0,
  output reg2_1,
  output reg2_2,
  output reg2_3,
  output reg3_0,
  output reg3_1,
  output reg3_2,
  output reg3_3,
  output inA_0,
  output inA_1,
  output inA_2,
  output inA_3,
  output inB_0,
  output inB_1,
  output inB_2,
  output inB_3,
  output out_40,
  output out_41,
  output out_42,
  output out_43
);

  wire counter_1_ovf, en_00, en_01, en_02, en_03, inAA_0, inAA_1, inAA_2, inAA_3, inM_00, inM_01, inM_02,
       inM_03, not_1_out, not_2_out;

  Demultiplexer #(.Selector_Bits(2)) demultiplexer_1 (
    .sel({sel_write_1, sel_write_0}), .in(1'b1), .out_0(en_00), .out_1(en_01), .out_2(en_02), .out_3(en_03));
  Register #(.Bits(4)) register_1 (.D({in3, in2, in1, in0}), .C(clk), .en(en_00), .Q({reg0_3, reg0_2, reg0_1, reg0_0}));
  Register #(.Bits(4)) register_2 (.D({in3, in2, in1, in0}), .C(clk), .en(en_01), .Q({reg1_3, reg1_2, reg1_1, reg1_0}));
  Register #(.Bits(4)) register_3 (.D({in3, in2, in1, in0}), .C(clk), .en(en_02), .Q({reg2_3, reg2_2, reg2_1, reg2_0}));
  Register #(.Bits(4)) register_4 (.D({in3, in2, in1, in0}), .C(clk), .en(en_03), .Q({reg3_3, reg3_2, reg3_1, reg3_0}));
  Register #(.Bits(4)) register_5 (.D({in3, in2, in1, in0}), .C(clk), .en(not_1_out), .Q({inA_3, inA_2, inA_1, inA_0}));
  not not_1 (not_1_out, counter_1_ovf);
  Register #(.Bits(4)) register_6 (
    .D({in3, in2, in1, in0}), .C(clk), .en(counter_1_ovf), .Q({inB_3, inB_2, inB_1, inB_0}));
  Register #(.Bits(4)) register_7 (
    .D({inA_3, inA_2, inA_1, inA_0}), .C(clk), .en(counter_1_ovf), .Q({inAA_3, inAA_2, inAA_1, inAA_0}));
  not not_2 (not_2_out, 1'b1);
  Counter counter_1 (.en(1'b1), .C(clk), .clr(not_2_out), .ovf(counter_1_ovf));  // open: out
  Multiplexer multiplexer_1 (.sel(inB_0), .in_0(inAA_0), .in_1(inAA_3), .out(inM_03));
  Multiplexer multiplexer_2 (.sel(inB_0), .in_0(inAA_1), .in_1(inAA_0), .out(inM_02));
  Multiplexer multiplexer_3 (.sel(inB_0), .in_0(inAA_2), .in_1(inAA_1), .out(inM_01));
  Multiplexer multiplexer_4 (.sel(inB_0), .in_0(inAA_3), .in_1(inAA_2), .out(inM_00));
  Multiplexer multiplexer_5 (.sel(inB_1), .in_0(inM_03), .in_1(inM_01), .out(out0));
  Multiplexer multiplexer_6 (.sel(inB_1), .in_0(inM_02), .in_1(inM_00), .out(out1));
  Multiplexer multiplexer_7 (.sel(inB_1), .in_0(inM_01), .in_1(inM_03), .out(out2));
  Multiplexer multiplexer_8 (.sel(inB_1), .in_0(inM_00), .in_1(inM_02), .out(out3));
  Seven_Seg_Hex seven_seg_hex_1 (.d({inA_3, inA_2, inA_1, inA_0}), .dp(1'b0));
  Seven_Seg_Hex seven_seg_hex_2 (.d({reg3_3, reg3_2, reg3_1, reg3_0}), .dp(1'b0));
  Seven_Seg_Hex seven_seg_hex_3 (.d({in3, in2, in1, in0}), .dp(1'b0));
  Seven_Seg_Hex seven_seg_hex_4 (.d({inB_3, inB_2, inB_1, inB_0}), .dp(1'b0));
  Seven_Seg_Hex seven_seg_hex_5 (.d({reg2_3, reg2_2, reg2_1, reg2_0}), .dp(1'b0));
  Seven_Seg_Hex seven_seg_hex_6 (.d({2'b00, sel_write_1, sel_write_0}), .dp(1'b0));
  Seven_Seg_Hex seven_seg_hex_7 (.d({2'b00, sel_readA_1, sel_readA_0}), .dp(1'b0));
  Seven_Seg_Hex seven_seg_hex_8 (.d({out3, out2, out1, out0}), .dp(1'b0));
  Seven_Seg_Hex seven_seg_hex_9 (.d({reg1_3, reg1_2, reg1_1, reg1_0}), .dp(1'b0));
  Seven_Seg_Hex seven_seg_hex_10 (.d({2'b00, sel_readB_1, sel_readB_0}), .dp(1'b0));
  Seven_Seg_Hex seven_seg_hex_11 (.d({reg0_3, reg0_2, reg0_1, reg0_0}), .dp(1'b0));

  assign out_40 = out3;
  assign out_41 = out2;
  assign out_42 = out1;
  assign out_43 = out0;

  // Other names for the same wires on the sheet: out_main[3:0] = {in3, in2, in1, in0}; inM_10 = out3; inM_11 = out2;
  //   inM_12 = out1; inM_13 = out0; ar_00[3:0] = {reg0_3, reg0_2, reg0_1, reg0_0};
  //   sel_00[3:0] = {reg0_3, reg0_2, reg0_1, reg0_0}; ar_01[3:0] = {reg1_3, reg1_2, reg1_1, reg1_0};
  //   sel_01[3:0] = {reg1_3, reg1_2, reg1_1, reg1_0}; ar_10[3:0] = {reg2_3, reg2_2, reg2_1, reg2_0};
  //   sel_10[3:0] = {reg2_3, reg2_2, reg2_1, reg2_0}; ar_11[3:0] = {reg3_3, reg3_2, reg3_1, reg3_0};
  //   sel_11[3:0] = {reg3_3, reg3_2, reg3_1, reg3_0}

  // Notes on the sheet:
  //   Design v2
  //   Interface (do not edit the content inside this box)
  //   Inputs
  //   Keypad
  //   Outputs
  //   Registers
  //   Values read into ALU inputs
  //   Rotatee
  //   Register 3
  //   Synchronizing Clock
  //   Rotation amount:
  //   Register Selection: Write-to
  //   Register 2
  //   Register Selection: Read-from
  //   ALU Output
  //   ALU input A register address:
  //   Register 1
  //   ALU input B register address:
  //   Register 0
endmodule

/* Test case:
clk in3 in2 in1 in0 sel^write_1 sel^write_0 sel^readA_1 sel^readA_0 sel^readB_1 sel^readB_0  reg3_3 reg3_2 reg3_1 reg3_0 reg2_3 reg2_2 reg2_1 reg2_0 reg1_3 reg1_2 reg1_1 reg1_0 reg0_3 reg0_2 reg0_1 reg0_0 out3 out2 out1 out0
 0   0   0   0   0   0           0           0           0           0           0            0      0      0      0      0      0      0      0      0      0      0      0      0      0      0      0      0    0    0    0
 1   0   0   0   0   0           0           0           0           0           0            0      0      0      0      0      0      0      0      0      0      0      0      0      0      0      0      0    0    0    0
 0   0   1   0   1   1           1           0           0           0           0            0      0      0      0      0      0      0      0      0      0      0      0      0      0      0      0      0    0    0    0
 1   0   1   0   1   1           1           0           0           0           0            0      1      0      1      0      0      0      0      0      0      0      0      0      0      0      0      0    0    0    0
 0   0   0   0   1   0           1           0           0           0           0            0      1      0      1      0      0      0      0      0      0      0      0      0      0      0      0      0    0    0    0
 1   0   0   0   1   0           1           0           0           0           0            0      1      0      1      0      0      0      0      0      0      0      1      0      0      0      0      0    0    0    0
 0   0   0   0   0   0           0           1           1           0           1            0      1      0      1      0      0      0      0      0      0      0      1      0      0      0      0      1    0    1    0
 1   0   0   0   0   0           0           1           1           0           1            0      1      0      1      0      0      0      0      0      0      0      1      0      0      0      0      1    0    1    0
 0   0   0   0   0   0           0           0           1           1           1            0      1      0      1      0      0      0      0      0      0      0      1      0      0      0      0      0    0    1    0
 1   0   0   0   0   0           0           0           1           1           1            0      1      0      1      0      0      0      0      0      0      0      1      0      0      0      0      0    0    1    0
*/
